# Fritzing sketch wiring-diagram (saved by Fritzing 0.9.4)
breadboards: 1

parts:
  Componente1 = Arduino Uno (Rev3)
  R1 = PHOTOCELL [package=photocell]
  R2 = Resistor [tolerance=±5% resistance=10k package=THT]
  DFRobot_DFPlayer_Mini1 = DFRobot DFPlayer Mini [part_number=DFR0299]
  SP1 = SPEAKER [package=pcb_mount_speaker]
  R3 = Resistor [tolerance=±5% resistance=1k package=THT]

nets:
  N1: Componente1.A0, R1.P$2, R2.Pin_1
  N2: Componente1.D10_PWM/SS, DFRobot_DFPlayer_Mini1.TX
  N3: Componente1.D11_PWM/MOSI, R3.Pin_0
  N4: Componente1.GND, R2.Pin_0, DFRobot_DFPlayer_Mini1.GND-1, DFRobot_DFPlayer_Mini1.GND-2
  5V: Componente1.5V, R1.P$1, DFRobot_DFPlayer_Mini1.VCC
  N5: DFRobot_DFPlayer_Mini1.RX, R3.Pin_1
  N6: DFRobot_DFPlayer_Mini1.SPK_1, SP1.-
  N7: DFRobot_DFPlayer_Mini1.SPK_2, SP1.+
